# Fritzing sketch BT_Relay (saved by Fritzing 0.9.2b)
breadboards: 1

parts:
  Часть1 = Bluetooth HC-06
  Часть2 = Arduino Leonardo (Rev3b)
  J1 = Screw terminal - 2 pins [package=THT]
  Q1 = NPN-Transistor [package="TO92 [THT]"]
  R1 = Resistor [tolerance=±5% resistance=10k package=THT]
  S1 = Pushbutton [package="[THT]"]
  J2 = Screw terminal - 2 pins [package=THT]
  R2 = Resistor [tolerance=±5% resistance=220 package=THT]

nets:
  N1: Часть1.RXD, Часть2.D1/TX
  N2: Часть1.TXD, Часть2.D0/RX
  GND: Часть1.GND, Часть2.GND, Q1.C, R1.Pin_1, J2.pin1
  VCC: Часть1.VCC, Часть2.3V3
  N3: Часть2.5V, S1.Pin_1, S1.Pin_2
  N4: Часть2.VIN, J2.pin2
  N5: Часть2.D10_PWM/A10, R1.Pin_0, S1.Pin_3, S1.Pin_4
  N6: Часть2.D13_PWM, R2.Pin_0
  N7: J1.pin2, Q1.E
  N8: Q1.B, R2.Pin_1
