# Fritzing sketch arduinoboard (saved by Fritzing 0.9.2b)
circuit board: 6.88566cm x 5.36311cm
breadboards: 1

parts:
  Arduino = Arduino Mini (Rev5)
  U1 = Voltage Regulator - 5V [package="TO220 [THT]"]
  C2 = Electrolytic Capacitor [capacitance=1µF package="100 mil [THT, electrolytic]"]
  C1 = Electrolytic Capacitor [capacitance=2.2µF package="100 mil [THT, electrolytic]"]
  Bluetooth_Bee = XBee [part_number=Bluettoth]
  J1 = Screw terminal - 2 pins [package=THT]
  IC1 = IC, DIP package, 6 pins [chip_label=IC part_number=КР293КП1Б]
  U2 = Voltage Regulator - 3.3V [package="TO220 [THT]"]
  C3 = Electrolytic Capacitor [capacitance=1µF package="100 mil [THT, electrolytic]"]
  S1 = Pushbutton [package="[THT]"]
  J2 = screw terminal, 3 pins
  IC = male pin header, 3 pins [form="♂ (male)"]
  SP = male pin header, 3 pins [form="♂ (male)"]
  R3 = Resistor [tolerance=±5% resistance=220 package=THT]
  R4 = Resistor [tolerance=±5% resistance=10k package=THT]

nets:
  N1: Arduino.D0/TX, Arduino.TX, Bluetooth_Bee.pin3
  N2: Arduino.D1/RX, Arduino.RX, Bluetooth_Bee.pin2
  N3: Arduino.RESET, IC.pin3
  GND: Arduino.GND, U1.GND, C2.-, C1.-, Bluetooth_Bee.GND, J1.pin1, IC1.pin1, U2.GND, C3.-, SP.pin3, R4.Pin_1
  N4: Arduino.D6_PWM, R3.Pin_0
  N5: Arduino.D8, Bluetooth_Bee.pin5
  5V/Vcc: Arduino.VCC, Arduino.5V, U1.output_voltage, C2.+, U2.input_voltage, S1.Pin_1, S1.Pin_2, SP.pin1
  N6: Arduino.D13, IC.pin2
  N7: Arduino.D12, IC.pin1
  N8: Arduino.D11_PWM, SP.pin2
  N9: Arduino.D10_PWM, S1.Pin_3, S1.Pin_4, R4.Pin_0
  12V: U1.input_voltage, C1.+, J1.pin2
  3.3V: Bluetooth_Bee.VCC, U2.output_voltage, C3.+
  N10: IC1.pin2, R3.Pin_1
  N11: IC1.pin4, J2.pin3
  N12: IC1.pin5, J2.pin2
  N13: IC1.pin6, J2.pin1

notes:
  http://kuleshov.msk.ru
  ICSP

// code stored in the sketch: bluetooth_relay.ino
#include <EEPROM.h>
#include <sha1.h> // https://github.com/Cathedrow/Cryptosuite

#define SESSION_KEY_LENGTH  20
#define SECRET_KEY_LENGTH  20
#define SESSION_TIMEOUT  20000 //ms

#define EEPROM_SECRET_OFFSET  20

#define RELAY_PIN  13
#define RELAY_COM_TIME  500 //ms

#define SETUPBUTTON_PIN  10

char secret[SECRET_KEY_LENGTH];// = "password";
unsigned long sessionStart = 0;
String sessionKey;

String message = "";

String printSessionKey(int passLength) {
  String result = "";
  for (int i = 0; i < passLength; i++) {
    result += "abcdefghijklmnopqrstuvwxyz0123456789ABCDEFGHIJKLMNOPQRSTUVWXYZ"[random(62)];
  }
  return result;
}

String printHash(uint8_t* hash) {
  String result = "";
  for (int i = 0; i < 20; i++) {
    result += "0123456789abcdef"[hash[i] >> 4];
    result += "0123456789abcdef"[hash[i] & 0xf];
  }
  return result;
}

void setup() {
  pinMode(RELAY_PIN, OUTPUT);
  pinMode(SETUPBUTTON_PIN, INPUT);
  EEPROM.get(EEPROM_SECRET_OFFSET, secret);
  Serial.begin(9600);
  //while (!Serial) {} // Leonagdo debug ONLY
  randomSeed(analogRead(A1));

  //Serial.println(secret);
}

void relayCom() { // main relay action
  digitalWrite(RELAY_PIN, HIGH);
  delay(RELAY_COM_TIME);
  digitalWrite(RELAY_PIN, LOW);
}

String commandProcessor(String incomingString) {
  String result;

  incomingString.trim();

  if (incomingString.startsWith("OPEN")) {
    sessionStart = millis();
    sessionKey = printSessionKey(SESSION_KEY_LENGTH);
    result = sessionKey;
  } else if (incomingString.startsWith("PASS:") && (millis() - sessionStart <= SESSION_TIMEOUT)) {
    incomingString.remove(0, incomingString.indexOf(":") + 1);
    Sha1.initHmac((const uint8_t*)secret, strlen(secret));
    Sha1.print(sessionKey);
    String ss = printHash(Sha1.resultHmac());
    //Serial.print("# "); Serial.println(ss);
    //Serial.print("< "); Serial.println(incomingString);
    if (incomingString.equalsIgnoreCase(ss)) {
      result = "OK";
      relayCom();
    } else {
      result = "NO";
    }
  } else if  (incomingString.startsWith("SECRET:") && digitalRead(SETUPBUTTON_PIN))  {
    incomingString.remove(0, incomingString.indexOf(":") + 1);
    incomingString.toCharArray(secret, SECRET_KEY_LENGTH);
    EEPROM.put(EEPROM_SECRET_OFFSET, secret);
    result = "OK";
  } else if  (incomingString.startsWith("BTNAME:") && digitalRead(SETUPBUTTON_PIN)) {
    result = "COMING_SOON";
  } else if  (incomingString.startsWith("BTPIN:") && digitalRead(SETUPBUTTON_PIN)) {
    result = "COMING_SOON";
  }
  else {
    result = "BLUETOOTH CRYPTO RELAY 0.1";
  }

  return result;
}

void loop() {

  if (Serial.available() > 0) {
    // read the incoming byte:
    char incomingChar = Serial.read();
    if (incomingChar == '\n') {
      Serial.println(commandProcessor(message));
      message = "";
    } else {
      message += incomingChar;
    }
  }
}
